# Fritzing sketch PotenciometerLed (saved by Fritzing 0.9.1b)
breadboards: 1

parts:
  R1 = Resistor [tolerance=±5% resistance=300 package="0603 [SMD]"]
  LED1 = LED - 5mm [color="Green (555nm)" package="5 mm [THT]"]
  Part1 = Arduino Uno (Rev3) - ICSP
  R2 = Rotary Potentiometer (Large) [maximum_resistance=10kΩ package=THT]

nets:
  N1: R1.Pin_0, LED1.anode
  N2: R1.Pin_1, Part1.D13/SCK
  N3: LED1.cathode, Part1.GND, R2.leg2
  N4: Part1.A0, R2.wiper
  N5: Part1.5V, R2.leg1
