# Fritzing sketch PotenciometerLedWithoutArduino (saved by Fritzing 0.9.1b)
breadboards: 1

parts:
  LED1 = LED - 5mm [color="Green (555nm)" package="5 mm [THT]"]
  Part1 = Arduino Uno (Rev3) - ICSP
  R2 = Rotary Potentiometer (Large) [maximum_resistance=10kΩ package=THT]
  R3 = Resistor [tolerance=±5% resistance=300 package="0603 [SMD]"]

nets:
  N1: LED1.cathode, Part1.GND, R2.leg1
  N2: LED1.anode, R3.Pin_0
  N3: Part1.5V, R2.leg2
  N4: R2.wiper, R3.Pin_1
