# Fritzing sketch barGraphTemperature (saved by Fritzing 0.9.1b)
breadboards: 1

parts:
  T1 = LM35 Temperature Sensor [package="TO92 [THT]"]
  Part1 = Arduino Uno (Rev3)
  D1 = LED_BARGRAPH_10 [package=led_bargaph_10]
  R1 = Resistor [tolerance=±5% resistance=300 package="0603 [SMD]"]

nets:
  N1: T1.+Vs, Part1.5V
  N2: T1.Vout, Part1.A0
  GND: T1.GND, Part1.GND
  N3: Part1.D8, D1.G_C
  N4: Part1.D9_PWM, D1.H_C
  N5: Part1.D10_PWM/SS, D1.I_C
  N6: Part1.D11_PWM/MOSI, D1.J_C
  N7: Part1.D2, D1.A_C
  N8: Part1.D3_PWM, D1.B_C
  N9: Part1.D4, D1.C_C
  N10: Part1.D5_PWM, D1.D_C
  N11: Part1.D6_PWM, D1.E_C
  N12: Part1.D7, D1.F_C
  N13: D1.A_A, D1.B_A, D1.C_A, D1.D_A, D1.E_A, D1.F_A, D1.G_A, D1.H_A, D1.I_A, D1.J_A, R1.Pin_1

// code stored in the sketch: barGraphTemperature.ino
#include<math.h>

//Variáveis do sensor de temperatura
const int sensorAnPin = 0;
const float maxReaderSize = pow(2, 10) - 1;		//10bits = 1024 (-1)
const int maxSensorTemperature = 110;			//Temperatura máxima do sensor (110ºC para 1.1V e 150ºC para > 1.5V)
float temperature = 0;							//Temperatura

//Variáveis do bargraph
const int bgPin[] = { 2, 3, 4, 5, 6, 7, 8, 9, 10, 11 };

void setup()
{
	Serial.begin(9600);			//Leitura SERIAL
	analogReference(INTERNAL);	//Limita a entra analógica para 1.1V

	for (int x = 0; x < 10; x++) {
		pinMode(bgPin[x], OUTPUT);
	}
}

void loop()
{
	//Busca resultado do ADC
	unsigned int sensorADC = analogRead(sensorAnPin);

	//Converte a leitura em temperatura (conversão direta regra de três)
	temperature = (maxSensorTemperature / maxReaderSize) * sensorADC;

	//Ascende a luz de acordo com a temperatura
	for (int x = 0; x < 10; x++) {
		if (round(temperature * 10) > 250 + (bgPin[x] * 5)) {
			digitalWrite(bgPin[x], HIGH);
		} else {
			digitalWrite(bgPin[x], LOW);
		}
	}

	//DEBUGs
	Serial.print("Temperatura: ");
	Serial.println(temperature);


}
